// Logisim project s-mips.circ as structural Verilog: 12 circuits, main circuit S-MIPS Board
module S_MIPS_Board (
  output halt
);

  wire button_1_out, CLK, CS, d_ff_1_q, R_W, Reset_out, RST, TTY_EN;
  wire [2:0] KDB;
  wire [3:0] Mask, ram_1_read_time, ram_1_write_time;
  wire [6:0] KDB_DATA, TTY_DATA;
  wire [15:0] Addr;
  wire [31:0] ram_1_data_out_0, ram_1_data_out_1, ram_1_data_out_2, ram_1_data_out_3, s_mips_1_ram_in_0,
       s_mips_1_ram_in_1, s_mips_1_ram_in_2, s_mips_1_ram_in_3;

  TTY #(.rows(25), .cols(80)) tty_1 (.data(TTY_DATA), .clk(CLK), .we(TTY_EN), .clr(RST));
  RAM ram_1 (
    .Address(Addr), .Data_Out_0(ram_1_data_out_0), .Data_Out_1(ram_1_data_out_1),
    .Data_Out_2(ram_1_data_out_2), .Data_Out_3(ram_1_data_out_3), .Data_In_0(s_mips_1_ram_in_0),
    .Data_In_1(s_mips_1_ram_in_1), .Data_In_2(s_mips_1_ram_in_2), .Data_In_3(s_mips_1_ram_in_3), .Mask(Mask),
    .nRead_Write(R_W), .Chip_Select(CS), .Read_Time(ram_1_read_time), .Reset(button_1_out),
    .Write_Time(ram_1_write_time));
  Button button_1 (.out(button_1_out));
  Keyboard #(.buflen(64)) keyboard_1 (.clk(CLK), .re(KDB[0]), .avail(KDB[2]), .data(KDB_DATA));  // open: clr
  S_MIPS s_mips_1 (
    .Kbd_Enable(KDB[0]), .Address(Addr), .Kbd_Clear(KDB[1]), .Kbd_Available(KDB[2]),
    .RAM_In_0(s_mips_1_ram_in_0), .Kbd_ASCII_Data(KDB_DATA), .RAM_In_1(s_mips_1_ram_in_1),
    .TTY_Enable(TTY_EN), .RAM_In_2(s_mips_1_ram_in_2), .RAM_In_3(s_mips_1_ram_in_3),
    .TTY_ASCII_Data(TTY_DATA), .Reset(RST), .RAM_Out_0(ram_1_data_out_0), .Clock(CLK),
    .RAM_Out_1(ram_1_data_out_1), .Stop(halt), .RAM_Out_2(ram_1_data_out_2), .RAM_Out_3(ram_1_data_out_3),
    .Mask(Mask), .Read_Time(ram_1_read_time), .Write_Time(ram_1_write_time), .nRead_Write(R_W),
    .Chip_Select(CS));
  D_Flip_Flop d_ff_1 (.clk(CLK), .D(1'b1), .Q(d_ff_1_q), .reset(Reset_out));  // open: Qn, preset, en
  Button Reset (.out(Reset_out));
  Clock clock_1 (.out(CLK));
  D_Flip_Flop d_ff_2 (.clk(CLK), .D(d_ff_1_q), .Qn(RST), .reset(Reset_out));  // open: Q, preset, en

  // Notes on the sheet:
  //   NO MODIFICAR
  //   Keyboard
endmodule

module RAM (
  input  [15:0] Address,
  input  [31:0] Data_In_0,
  input  [31:0] Data_In_1,
  input  [31:0] Data_In_2,
  input  [31:0] Data_In_3,
  input  [3:0] Mask,
  input  nRead_Write,
  input  Chip_Select,
  input  Reset,
  output [31:0] Data_Out_0,
  output [31:0] Data_Out_1,
  output [31:0] Data_Out_2,
  output [31:0] Data_Out_3,
  output [3:0] Read_Time,
  output [3:0] Write_Time
);

  wire and_2_out, and_3_out, and_4_out, and_5_out, and_6_out, and_7_out, and_8_out, and_9_out, Changed, CLK,
       comparator_2_eq, comparator_3_eq, comparator_4_eq, comparator_5_eq, comparator_6_eq, Count,
       demultiplexer_3_out0, Idle, Idle_q, Load, Load0, Load1, nand_1_out, or_1_out, or_2_out, or_3_out,
       or_4_out, or_5_out, or_6_out, or_7_out, or_8_out, or_9_out, or_10_out, Proc_q, Update_Mem, Zero_Time;
  wire [3:0] counter_1_q, multiplexer_1_out, subtractor_1_out;
  wire [31:0] register_1_q, register_2_q, register_3_q, register_4_q, register_5_q;

  // Probe on 4'b0011
  // Probe on 4'b0101
  Multiplexer #(.width(4), .enable("false")) multiplexer_1 (
    .in0(4'b0011), .in1(4'b0101), .out(multiplexer_1_out), .sel(nRead_Write));
  or or_1 (or_1_out, Idle, Update_Mem);
  or or_2 (or_2_out, ~Chip_Select, Reset);  // OR_Gate
  Subtractor #(.width(4)) subtractor_1 (.a(multiplexer_1_out), .b(4'b0010), .out(subtractor_1_out));  // open: bin, bout
  Demultiplexer #(.enable("false")) demultiplexer_1 (.out0(Idle), .out1(Load0), .in(Idle_q), .sel(Changed));
  D_Flip_Flop u_Idle (.clk(CLK), .D(or_1_out), .Q(Idle_q), .preset(or_2_out));  // open: Qn, en, reset
  // Probe on counter_1_q
  Counter #(.width(4), .max('hf)) counter_1 (
    .load(Load), .D(subtractor_1_out), .count(Count), .Q(counter_1_q), .clk(CLK), .clr(or_3_out));  // open: carry
  or or_3 (or_3_out, ~Chip_Select, Reset);  // OR_Gate
  Comparator #(.width(4), .mode("unsigned")) comparator_1 (
    .a(4'b0000), .b(counter_1_q), .eq(Zero_Time));  // open: gt, lt
  or or_4 (or_4_out, Count, Load0, Load1);
  Register #(.width(32)) register_1 (.D(Data_In_0), .en(Chip_Select), .Q(register_1_q), .clk(CLK), .clr(or_5_out));
  or or_5 (or_5_out, ~Chip_Select, Reset);  // OR_Gate
  Register #(.width(32)) register_2 (.D(Data_In_1), .en(Chip_Select), .Q(register_2_q), .clk(CLK), .clr(or_6_out));
  or or_6 (or_6_out, ~Chip_Select, Reset);  // OR_Gate
  Register #(.width(32)) register_3 (.D(Data_In_2), .en(Chip_Select), .Q(register_3_q), .clk(CLK), .clr(or_7_out));
  or or_7 (or_7_out, ~Chip_Select, Reset);  // OR_Gate
  Register #(.width(32)) register_4 (.D(Data_In_3), .en(Chip_Select), .Q(register_4_q), .clk(CLK), .clr(or_8_out));
  or or_8 (or_8_out, ~Chip_Select, Reset);  // OR_Gate
  Register #(.width(32)) register_5 (
    .D({{11{1'b1}}, nRead_Write, Mask, Address}), .en(Chip_Select), .Q(register_5_q), .clk(CLK),
    .clr(or_9_out));
  or or_9 (or_9_out, ~Chip_Select, Reset);  // OR_Gate
  D_Flip_Flop Proc (.clk(CLK), .D(or_4_out), .Q(Proc_q), .reset(or_10_out));  // open: Qn, preset, en
  or or_10 (or_10_out, ~Chip_Select, Reset);  // OR_Gate
  Demultiplexer #(.enable("false")) demultiplexer_2 (
    .out0(Count), .out1(Update_Mem), .in(demultiplexer_3_out0), .sel(Zero_Time));
  Demultiplexer #(.enable("false")) demultiplexer_3 (
    .out0(demultiplexer_3_out0), .out1(Load1), .in(Proc_q), .sel(Changed));
  Clock clock_1 (.out(CLK));
  Comparator #(.width(32)) comparator_2 (.a(register_1_q), .b(Data_In_0), .eq(comparator_2_eq));  // open: gt, lt
  Comparator #(.width(32)) comparator_3 (.a(register_2_q), .b(Data_In_1), .eq(comparator_3_eq));  // open: gt, lt
  Comparator #(.width(32)) comparator_4 (.a(register_3_q), .b(Data_In_2), .eq(comparator_4_eq));  // open: gt, lt
  Comparator #(.width(32)) comparator_5 (.a(register_4_q), .b(Data_In_3), .eq(comparator_5_eq));  // open: gt, lt
  Comparator #(.width(32)) comparator_6 (
    .a(register_5_q), .b({{11{1'b1}}, nRead_Write, Mask, Address}), .eq(comparator_6_eq));  // open: gt, lt
  nand nand_1 (nand_1_out, comparator_6_eq, comparator_2_eq, comparator_3_eq, comparator_4_eq, comparator_5_eq);
  and and_1 (Changed, nand_1_out, Chip_Select);
  or or_11 (Load, Count, Load1, Load0);
  and and_2 (and_2_out, Mask[0], Update_Mem, nRead_Write);
  and and_3 (and_3_out, Mask[1], Update_Mem, nRead_Write);
  and and_4 (and_4_out, Mask[2], Update_Mem, nRead_Write);
  and and_5 (and_5_out, Mask[3], Update_Mem, nRead_Write);
  RAM_part #(.addrWidth(16), .dataWidth(32), .bus("separate")) ram_1 (
    .addr(Address), .din(Data_In_0), .data(Data_Out_0), .str(and_2_out), .sel(Chip_Select), .clk(CLK),
    .ld(and_6_out), .clr(Reset));
  and and_6 (and_6_out, ~nRead_Write, Idle);  // AND_Gate
  RAM_part #(.addrWidth(16), .dataWidth(32), .bus("separate")) ram_2 (
    .addr(Address), .din(Data_In_1), .data(Data_Out_1), .str(and_3_out), .sel(Chip_Select), .clk(CLK),
    .ld(and_7_out), .clr(Reset));
  and and_7 (and_7_out, ~nRead_Write, Idle);  // AND_Gate
  RAM_part #(.addrWidth(16), .dataWidth(32), .bus("separate")) ram_3 (
    .addr(Address), .din(Data_In_2), .data(Data_Out_2), .str(and_4_out), .sel(Chip_Select), .clk(CLK),
    .ld(and_8_out), .clr(Reset));
  and and_8 (and_8_out, ~nRead_Write, Idle);  // AND_Gate
  RAM_part #(.addrWidth(16), .dataWidth(32), .bus("separate")) ram_4 (
    .addr(Address), .din(Data_In_3), .data(Data_Out_3), .str(and_5_out), .sel(Chip_Select), .clk(CLK),
    .ld(and_9_out), .clr(Reset));
  and and_9 (and_9_out, ~nRead_Write, Idle);  // AND_Gate

  assign Read_Time = 4'b0011;
  assign Write_Time = 4'b0101;

  // Other names for the same wires on the sheet: M0 = Mask[0]; M1 = Mask[1]; M2 = Mask[2]; M3 = Mask[3];
  //   RW = nRead_Write; CLR = Reset; CS = Chip_Select; Load2 = Count

  // Notes on the sheet:
  //   NO MODIFICAR
  //   excepto quizás los valores RT y WT
  //   BANK0
  //   BANK1
  //   BANK2
  //   BANK3
endmodule

module S_MIPS (
  input  Kbd_Available,
  input  [6:0] Kbd_ASCII_Data,
  input  [31:0] RAM_Out_0,
  input  [31:0] RAM_Out_1,
  input  Reset,
  input  [31:0] RAM_Out_2,
  input  Clock,
  input  [31:0] RAM_Out_3,
  input  [3:0] Read_Time,
  input  [3:0] Write_Time,
  output Kbd_Enable,
  output [15:0] Address,
  output Kbd_Clear,
  output TTY_Enable,
  output [6:0] TTY_ASCII_Data,
  output Stop,
  output nRead_Write,
  output Chip_Select,
  output [31:0] RAM_In_0,
  output [31:0] RAM_In_1,
  output [31:0] RAM_In_2,
  output [31:0] RAM_In_3,
  output [3:0] Mask
);

  wire add, addi, alu, \and , and_2_out, and_3_out, andi, beq, bgtz, blez, bltz, bneq, CLK, CS_1, CS_2,
       cu_beq, cu_bgtz, cu_blez, cu_bltz, cu_bneq, cu_enInstruction, cu_enMemRead, cu_enMemWrite, cu_enR_W,
       cu_enRandom, cu_enSP, cu_j, cu_jr, cu_popRF, cu_pushRF, cu_sign, div, divu, en_pc_NextInst, flag_neg,
       flag_zero, halt, Hi_Lo_enable, inst_ready, InstEnab, jr, jump, keyboard, lw, mem, mfhi, mflo, minus_1,
       mult, mulu, next, nop, \nor , \or , or_1_out, or_2_out, or_4_out, or_5_out, or_13_out, ori, pop, push,
       random_t, RD, ready_mem, ready_read, ready_write, ReadyIC, SelD2, slt, slti, sltiu, sltu, sub, sw,
       tty, \xor , xori, zero;
  wire [2:0] cu_op_selector, DS;
  wire [4:0] multiplexer_6_out, sel_Rd, sel_Rs, sel_Rt;
  wire [5:0] func_code, op_code;
  wire [15:0] InstructionAddress, MH_Address;
  wire [25:0] dest;
  wire [31:0] adder_1_out, ALU_result, cte, Dir, eq, gtz, Hi, Hi_inRF, INST_CACHE_OUT__0, INST_CACHE_OUT__1,
       INST_CACHE_OUT__2, INST_CACHE_OUT__3, Instruction, KBD_Data_extended, lez, Lo, Lo_inRF, ltz, MH_data,
       multiplexer_4_out, multiplexer_5_out, multiplexer_7_out, multiplexer_8_out, neq, pc_in, pc_out,
       Random, register_file_1_instruction, Rt, slt_result, sltu_result, SP, write_data;
  wire [31:7] Rs;

  // Probe on SP
  Adder #(.width(32)) adder_1 (.a({Rs, TTY_ASCII_Data}), .b(cte), .out(adder_1_out));  // open: cin, cout
  Multiplexer #(.width(32), .enable("false")) multiplexer_1 (.in0(adder_1_out), .in1(SP), .out(Dir), .sel(or_1_out));
  or or_1 (or_1_out, push, pop);
  Multiplexer #(.width(32), .enable("false")) multiplexer_2 (
    .in0(Rt), .in1({Rs, TTY_ASCII_Data}), .out(write_data), .sel(push));
  and and_1 (CLK, Clock, ~Stop);  // AND_Gate
  Memory_Handler memory_handler_1 (
    .ReadTime(Read_Time), .enRead(cu_enMemRead), .clear(Reset), .clk(CLK), .CS_R(CS_2), .FinishR(ready_read),
    .Write_Time(Write_Time), .enWrite(cu_enMemWrite), .FinishW(ready_write), .RAM_Out_0(RAM_Out_0),
    .RAM_Out_1(RAM_Out_1), .RAM_Out_2(RAM_Out_2), .RAM_Out_3(RAM_Out_3), .Dir(Dir), .DataOut(MH_data),
    .Value(write_data), .RAM_Input_1(RAM_In_0), .mask(Mask), .RAM_Input_2(RAM_In_1), .address(MH_Address),
    .RAM_Input_3(RAM_In_2), .RAM_Input_4(RAM_In_3), .CS_W(nRead_Write));
  or or_2 (or_2_out, cu_enMemWrite, cu_pushRF);
  Instruction_Cache instruction_cache_1 (
    .Address(pc_out), .enable(InstEnab), .clear(Reset), .clk(CLK), .RAM_Out_0(RAM_Out_0),
    .RAM_Out_1(RAM_Out_1), .RAM_Out_2(RAM_Out_2), .RAM_Out_3(RAM_Out_3), .ReadTime(Read_Time),
    .CacheOut0(INST_CACHE_OUT__0), .CacheOut1(INST_CACHE_OUT__1), .CacheOut2(INST_CACHE_OUT__2),
    .CacheOut3(INST_CACHE_OUT__3), .AddressOut(InstructionAddress), .CS(CS_1), .Finish(ReadyIC));
  or or_3 (Chip_Select, CS_1, CS_2, nRead_Write);
  Multiplexer #(.width(16), .enable("false")) multiplexer_3 (
    .in0(MH_Address), .in1(InstructionAddress), .out(Address), .sel(CS_1));
  or or_4 (or_4_out, cu_enInstruction, Reset);
  and and_2 (and_2_out, cu_enMemRead, ~ready_read);  // AND_Gate
  or or_5 (or_5_out, and_2_out, and_3_out);
  and and_3 (and_3_out, or_2_out, ~ready_write);  // AND_Gate
  // Probe on Address
  and and_4 (InstEnab, or_4_out, ~or_5_out);  // AND_Gate
  Instruction_Fetcher instruction_fetcher_1 (
    .ram_in_1(INST_CACHE_OUT__0), .ram_in_2(INST_CACHE_OUT__1), .ram_in_3(INST_CACHE_OUT__2),
    .ram_in_4(INST_CACHE_OUT__3), .pc_out(pc_out), .out_9(Instruction), .Ready(ReadyIC), .Finish(inst_ready),
    .clk(CLK), .clr(Reset));
  or or_6 (alu, div, andi, addi, add, sub, mult, mulu, divu, \and , \or , \nor , ori, xori, \xor );
  assign KBD_Data_extended = {{25{1'b0}}, Kbd_ASCII_Data};  // Bit_Extender bit_extender_1
  and and_5 (minus_1, ~Kbd_Available, keyboard);  // AND_Gate
  or or_7 (mem, pop, lw);
  Branch_Control_Unit branch_control_unit_1 (
    .cu_beq(cu_beq), .cu_bne(cu_bneq), .cu_blez(cu_blez), .cu_bgtz(cu_bgtz), .cu_bltz(cu_bltz), .cu_j(cu_j),
    .cu_jr(cu_jr), .Next(en_pc_NextInst), .Dest(dest), .Offset(cte), .RS({Rs, TTY_ASCII_Data}),
    .PC_in(pc_out), .PC_Out(pc_in), .eq(eq), .neq(neq), .lez(lez), .gtz(gtz), .ltz(ltz));
  Control_Unit control_unit_1 (
    .nop(nop), .divu(divu), .pop(pop), .halt(halt), .andi(andi), .sw(sw), .ready_mem(ready_mem),
    .ready_inst(inst_ready), .add(add), .\and (\and ), .slt(slt), .kbd(keyboard), .ori(ori), .beq(beq),
    .CLK(CLK), .sub(sub), .\or (\or ), .sltu(sltu), .rnd(random_t), .xori(xori), .bne(bneq), .mul(mult),
    .\nor (\nor ), .jr(jr), .tty(tty), .slti(slti), .blez(blez), .Next(next), .mulu(mulu), .\xor (\xor ),
    .mfhi(mfhi), .j(jump), .sltiu(sltiu), .bgtz(bgtz), .OpCode(cu_op_selector), .div(div), .push(push),
    .mflo(mflo), .addi(addi), .lw(lw), .bltz(bltz), .Sign(cu_sign), .beq_2(cu_beq), .bne_2(cu_bneq),
    .blez_2(cu_blez), .bgtz_2(cu_bgtz), .bltz_2(cu_bltz), .j_2(cu_j), .jr_2(cu_jr), .enRND(cu_enRandom),
    .STOP(Stop), .enRead(cu_enMemRead), .enWrite(cu_enMemWrite), .pushRF(cu_pushRF), .popRF(cu_popRF),
    .enSP(cu_enSP), .R_W(cu_enR_W), .InstEnab(cu_enInstruction), .TTYEnab(TTY_Enable), .KBDEnab(Kbd_Enable));
  or or_8 (ready_mem, ready_read, ready_write);
  Multiplexer #(.width(32), .enable("false")) multiplexer_4 (
    .in0(sltu_result), .in1(slt_result), .out(multiplexer_4_out), .sel(cu_sign));
  or or_9 (DS[2], mflo, keyboard, mem, minus_1);
  or or_10 (DS[1], keyboard, minus_1, alu, mfhi);
  Multiplexer #(.select(3), .width(32), .enable("false")) multiplexer_5 (
    .in0(multiplexer_4_out), .in1(Random), .in2(ALU_result), .in3(Hi), .in4(Lo), .in5(MH_data),
    .in6(KBD_Data_extended), .in7({32{1'b1}}), .out(multiplexer_5_out), .sel(DS));
  or or_11 (en_pc_NextInst, next, ready_mem);
  and and_6 (Hi_Lo_enable, cu_op_selector[1], cu_op_selector[2]);
  or or_12 (DS[0], mfhi, random_t, mem, minus_1);
  Multiplexer #(.width(5), .enable("false")) multiplexer_6 (
    .in0(sel_Rt), .in1(sel_Rd), .out(multiplexer_6_out), .sel(RD));
  and and_7 (RD, or_13_out, ~SelD2);  // AND_Gate
  or or_13 (or_13_out, sltu, pop, keyboard, mflo, alu, random_t, mfhi, slt);
  Register_File register_file_1 (
    .DI(multiplexer_5_out), .clock(CLK), .reset(Reset), .DA(multiplexer_6_out), .S_a(sel_Rs), .S_b(sel_Rt),
    .A({Rs, TTY_ASCII_Data}), .B(Rt), .SP_Out(SP), .Lo(Lo_inRF), .Lo_2(Lo), .Hi(Hi_inRF), .Hi_2(Hi),
    .PC_Out(pc_out), .Instruction(register_file_1_instruction), .Random(Random), .loHi_en(Hi_Lo_enable),
    .inst_en(ReadyIC), .sp_en(cu_enSP), .pc_en(en_pc_NextInst), .rw_en(cu_enR_W), .push(cu_pushRF),
    .pop(cu_popRF), .random_en(cu_enRandom), .I_IN(Instruction), .PC_IN(pc_in));
  // Probe on pc_out
  // Probe on {Rs, TTY_ASCII_Data}
  // Probe on register_file_1_instruction
  or or_14 (SelD2, addi, andi, ori, xori, slti, sltiu);
  Arithmetic_Logic_Unit arithmetic_logic_unit_1 (
    .A({Rs, TTY_ASCII_Data}), .B(multiplexer_8_out), .result(ALU_result), .flag_neg(flag_neg),
    .flag_zero(flag_zero), .sign(cu_sign), .Op(cu_op_selector), .Hi(Hi_inRF), .Lo(Lo_inRF), .slt(slt_result),
    .sltu(sltu_result), .eq(eq), .neq(neq), .gtz(gtz), .lez(lez), .ltz(ltz));
  Instruction_Decoder instruction_decoder_1 (
    .in_1(register_file_1_instruction), .J(dest), .RS(sel_Rs), .RD(sel_Rd), .RT(sel_Rt), .jump(jump),
    .mfhi(mfhi), .mflo(mflo), .bneq(bneq), .bgtz(bgtz), .beq(beq), .blez(blez), .bltz(bltz), .push(push),
    .pop(pop), .lw(lw), .sw(sw), .nop(nop), .halt(halt), .random(random_t), .tty(tty), .keyboard(keyboard),
    .jr(jr), .func_code(func_code), .op_code(op_code), .add(add), .sub(sub), .mult(mult), .mulu(mulu),
    .div(div), .divu(divu), .sltu(sltu), .slt(slt), .\and (\and ), .\or (\or ), .\nor (\nor ), .\xor (\xor ),
    .addi(addi), .slti(slti), .ori(ori), .xori(xori), .andi(andi), .cte(cte), .sltiu(sltiu));
  Multiplexer #(.width(32), .enable("false")) multiplexer_7 (.in0(Rt), .in1(cte), .out(multiplexer_7_out), .sel(SelD2));
  Multiplexer #(.width(32), .enable("false")) multiplexer_8 (
    .in0(multiplexer_7_out), .in1({32{1'b0}}), .out(multiplexer_8_out), .sel(zero));
  or or_15 (zero, blez, bgtz, bltz);

  assign Kbd_Clear = Reset;

  // Other names for the same wires on the sheet: CS = Chip_Select; KBD_AVAIL = Kbd_Available; CLR = Reset;
  //   KBD_CLR = Reset; KBD_DATA[6:0] = Kbd_ASCII_Data; RAM_A[15:0] = Address; RAM_INPUT_0[31:0] = RAM_In_0;
  //   RAM_INPUT_1[31:0] = RAM_In_1; RAM_INPUT_2[31:0] = RAM_In_2; RAM_INPUT_3[31:0] = RAM_In_3; RAM_MASK[3:0] = Mask;
  //   RAM_OUTPUT_0[31:0] = RAM_Out_0; RAM_OUTPUT_1[31:0] = RAM_Out_1; RAM_OUTPUT_2[31:0] = RAM_Out_2;
  //   RAM_OUTPUT_3[31:0] = RAM_Out_3; Rs[6:0] = TTY_ASCII_Data; TTY_DATA[6:0] = TTY_ASCII_Data; CS_3 = nRead_Write;
  //   RW = nRead_Write

  // Notes on the sheet:
  //   RAM ADDRESS
  //   DATA FROM RAM
  //   DATA TO RAM
  //   DATA WRITE MASK
  //   RAM TIMING
  //   KEYBOARD
  //   TTY
  //   SEQUENCING
  //   RAM CONTROL
  //   TTY
  //   Esto lo tienen que borrar:
  //   Data Path
endmodule

module Arithmetic_Logic_Unit (
  input  [31:0] A,
  input  [31:0] B,
  input  sign,
  input  [2:0] Op,
  output [31:0] result,
  output flag_neg,
  output flag_zero,
  output [31:0] slt,
  output [31:0] sltu,
  output [31:0] Hi,
  output [31:0] eq,
  output [31:0] Lo,
  output [31:0] neq,
  output [31:0] gtz,
  output [31:0] lez,
  output [31:0] ltz
);

  wire adder_3_cout, and_1_out, and_2_out, C2, Hi_Lo_enable, NotPairs, Odds;
  wire [31:0] A_C2, adder_1_out, adder_2_out, and_4_out, B_C2, Div, end_Div, end_Mul_U, end_Up_Mul_U,
       LoMul_end, Mul, multiplexer_1_out, multiplexer_2_out, multiplexer_4_out, multiplexer_5_out,
       multiplexer_6_out, multiplexer_7_out, Mulu_Hi, Mulu_Lo, negator_2_out, not_1_out, or_2_out, Rem,
       subtractor_1_out, subtractor_2_out, Up_Mul, UpMul_end, xor_2_out;

  Negator #(.width(32)) negator_1 (.in(A), .out(A_C2));
  and and_1 (and_1_out, A[31], sign);
  Multiplexer #(.width(32), .enable("false")) multiplexer_1 (
    .in0(A), .in1(A_C2), .out(multiplexer_1_out), .sel(and_1_out));
  Multiplexer #(.width(32), .enable("false")) multiplexer_2 (
    .in0(B), .in1(B_C2), .out(multiplexer_2_out), .sel(and_2_out));
  and and_2 (and_2_out, sign, B[31]);
  Negator #(.width(32)) negator_2 (.in(Div), .out(negator_2_out));
  xor xor_1 (C2, A[31], B[31]);
  Divider #(.width(32)) divider_1 (.a(multiplexer_1_out), .b(multiplexer_2_out), .out(Div), .rem(Rem));  // open: upper
  Multiplexer #(.width(32), .enable("false")) multiplexer_3 (.in0(Div), .in1(negator_2_out), .out(end_Div), .sel(C2));
  and and_3 (Odds, A[0], B[0]);
  or or_1 (NotPairs, A[0], B[0]);
  Negator #(.width(32)) negator_3 (.in(B), .out(B_C2));
  Subtractor #(.width(32)) subtractor_1 (.a(A), .b(32'h1), .out(subtractor_1_out));  // open: bin, bout
  Adder #(.width(32)) adder_1 (.a(A), .b(B), .out(adder_1_out));  // open: cin, cout
  Subtractor #(.width(32)) subtractor_2 (.a(A), .b(B), .out(subtractor_2_out));  // open: bin, bout
  assign and_4_out = A & B;  // AND_Gate and_4, 32 bits wide
  assign not_1_out = ~or_2_out;  // NOT_Gate not_1, 32 bits wide
  assign or_2_out = A | B;  // OR_Gate or_2, 32 bits wide
  assign xor_2_out = A ^ B;  // XOR_Gate xor_2, 32 bits wide
  // Probe on end_Div
  Adder #(.width(32)) adder_2 (.a(subtractor_1_out), .b(B), .out(adder_2_out));  // open: cin, cout
  Multiplexer #(.width(32), .enable("false")) multiplexer_4 (.in0(A), .in1(B), .out(multiplexer_4_out), .sel(A[0]));
  Multiplexer #(.width(32), .enable("false")) multiplexer_5 (
    .in0({1'b0, A[31:1]}), .in1(A), .out(multiplexer_5_out), .sel(sign));
  Multiplier #(.width(32)) multiplier_1 (
    .a(multiplexer_5_out), .b(multiplexer_6_out), .out(Mul), .cout(Up_Mul));  // open: cin
  Multiplexer #(.width(32), .enable("false")) multiplexer_6 (
    .in0({1'b0, B[31:1]}), .in1(B), .out(multiplexer_6_out), .sel(sign));
  Multiplexer #(.width(32), .enable("false")) multiplexer_7 (
    .in0(multiplexer_4_out), .in1(adder_2_out), .out(multiplexer_7_out), .sel(Odds));
  Adder #(.width(32)) adder_3 (
    .a(multiplexer_7_out), .b({Mul[29:0], 2'b00}), .out(end_Mul_U), .cout(adder_3_cout));  // open: cin
  Adder #(.width(32)) adder_4 (
    .a({Up_Mul[29:0], Mul[31:30]}), .b({32{1'b0}}), .out(end_Up_Mul_U), .cin(adder_3_cout));  // open: cout
  Multiplexer #(.select(3), .width(32), .enable("false")) multiplexer_8 (
    .in0(adder_1_out), .in1(subtractor_2_out), .in2(and_4_out), .in3(not_1_out), .in4(or_2_out),
    .in5(xor_2_out), .in6(Mul), .in7(Div), .out({flag_neg, result[30:0]}), .sel(Op));
  and and_5 (Hi_Lo_enable, Op[1], Op[2]);
  Multiplexer #(.width(32), .enable("false")) multiplexer_9 (
    .in0({Mul[29:0], 2'b00}), .in1(end_Mul_U), .out(Mulu_Lo), .sel(NotPairs));
  Multiplexer #(.width(32), .enable("false")) multiplexer_10 (
    .in0({Up_Mul[29:0], Mul[31:30]}), .in1(end_Up_Mul_U), .out(Mulu_Hi), .sel(NotPairs));
  Multiplexer #(.width(32)) multiplexer_11 (.in0(UpMul_end), .in1(Rem), .out(Hi), .sel(Op[0]), .en(Hi_Lo_enable));
  Multiplexer #(.width(32)) multiplexer_12 (.in0(LoMul_end), .in1(end_Div), .out(Lo), .sel(Op[0]), .en(Hi_Lo_enable));
  Multiplexer #(.width(32), .enable("false")) multiplexer_13 (.in0(Mulu_Lo), .in1(Mul), .out(LoMul_end), .sel(sign));
  Multiplexer #(.width(32), .enable("false")) multiplexer_14 (.in0(Mulu_Hi), .in1(Up_Mul), .out(UpMul_end), .sel(sign));
  nor nor_1 (flag_zero, result[0], result[1], result[2], result[3], result[4], result[5], result[6], result[7], result[8], result[9], result[10], result[11], result[12], result[13], result[14], result[15], result[16], result[17], result[18], result[19], result[20], result[21], result[22], result[23], result[24], result[25], result[26], result[27], result[28], result[29], result[30], flag_neg);
  Comparator #(.width(32)) comparator_1 (.a(A), .b(B), .gt(gtz[0]), .eq(eq[0]), .lt(ltz[0]));
  Comparator #(.width(32), .mode("unsigned")) comparator_2 (.a(A), .b(B), .lt(sltu[0]));  // open: gt, eq
  not not_2 (neq[0], eq[0]);
  or or_3 (lez[0], eq[0], ltz[0]);

  assign eq[31:1] = {31{1'b0}};
  assign gtz[31:1] = {31{1'b0}};
  assign lez[31:1] = {31{1'b0}};
  assign ltz[31:1] = {31{1'b0}};
  assign neq[31:1] = {31{1'b0}};
  assign result[31] = flag_neg;
  assign slt = {{31{1'b0}}, ltz[0]};
  assign sltu[31:1] = {31{1'b0}};

  // Other names for the same wires on the sheet: _1A = A[0]; A1[30:0] = A[31:1]; SignA = A[31]; _1B = B[0];
  //   B1[30:0] = B[31:1]; SignB = B[31]; Up_Mul_U[31:0] = {Up_Mul[29:0], Mul[31:30]}; Mul_U[31:2] = Mul[29:0];
  //   Mult_Div = Op[0]

  // Notes on the sheet:
  //   Inputs
  //   Div
  //   add
  //   sub
  //   and
  //   nor
  //   or
  //   xor
  //   mul
  //   div
  //   Mul
  //   Hi/Lo Outputs
  //   slt
  //   sltu
  //   eq
  //   neq
  //   gtz
  //   lez
  //   ltz
  //   Branch Outputs
  //   Result
  //   Flag Outputs
endmodule

module Register_File (
  input  [31:0] DI,
  input  [4:0] DA,
  input  [4:0] S_a,
  input  [4:0] S_b,
  input  clock,
  input  reset,
  input  rw_en,
  input  pc_en,
  input  sp_en,
  input  inst_en,
  input  loHi_en,
  input  random_en,
  input  push,
  input  pop,
  input  [31:0] PC_IN,
  input  [31:0] I_IN,
  input  [31:0] Lo,
  input  [31:0] Hi,
  output [31:0] A,
  output [31:0] B,
  output [31:0] SP_Out,
  output [31:0] PC_Out,
  output [31:0] Instruction,
  output [31:0] Random,
  output [31:0] Lo_2,
  output [31:0] Hi_2
);

  wire L1, L2, L3, L4, L5, L6, L7, L8, L9, L10, L11, L12, L13, L14, L15, L16, L17, L18, L19, L20, L21, L22,
       L23, L24, L25, L26, L27, L28, L29, L30, L31, or_1_out, or_2_out;
  wire [31:0] adder_1_out, multiplexer_1_out, multiplexer_2_out, Q0, Q1, Q2, Q3, Q4, Q5, Q6, Q7, Q8, Q9, Q10,
       Q11, Q12, Q13, Q14, Q15, Q16, Q17, Q18, Q19, Q20, Q21, Q22, Q23, Q24, Q25, Q26, Q27, Q28, Q29, Q30,
       subtractor_1_out;

  Demultiplexer #(.select(5), .enable("false")) demultiplexer_1 (
    .out1(L1), .out2(L2), .out3(L3), .out4(L4), .out5(L5), .out6(L6), .out7(L7), .out8(L8), .out9(L9),
    .out10(L10), .out11(L11), .out12(L12), .out13(L13), .out14(L14), .out15(L15), .out16(L16), .out17(L17),
    .out18(L18), .out19(L19), .out20(L20), .out21(L21), .out22(L22), .out23(L23), .out24(L24), .out25(L25),
    .out26(L26), .out27(L27), .out28(L28), .out29(L29), .out30(L30), .out31(L31), .in(rw_en), .sel(DA));  // open: out0
  Adder #(.width(32)) adder_1 (.a(SP_Out), .b(32'h4), .out(adder_1_out));  // open: cin, cout
  Subtractor #(.width(32)) subtractor_1 (.a(SP_Out), .b(32'h4), .out(subtractor_1_out));  // open: bin, bout
  Multiplexer #(.width(32), .enable("false")) multiplexer_1 (
    .in0(adder_1_out), .in1(subtractor_1_out), .out(multiplexer_1_out), .sel(push));
  Multiplexer #(.width(32), .enable("false")) multiplexer_2 (
    .in0(SP_Out), .in1(multiplexer_1_out), .out(multiplexer_2_out), .sel(or_1_out));
  or or_1 (or_1_out, pop, push);
  or or_2 (or_2_out, sp_en, L31);
  Register #(.width(32)) R0 (.D({32{1'b0}}), .Q(Q0), .clk(clock), .clr(reset));  // open: en
  Register #(.width(32)) R1 (.D(DI), .en(L1), .Q(Q1), .clk(clock), .clr(reset));
  Register #(.width(32)) R2 (.D(DI), .en(L2), .Q(Q2), .clk(clock), .clr(reset));
  Register #(.width(32)) R3 (.D(DI), .en(L3), .Q(Q3), .clk(clock), .clr(reset));
  Register #(.width(32)) R4 (.D(DI), .en(L4), .Q(Q4), .clk(clock), .clr(reset));
  Register #(.width(32)) R5 (.D(DI), .en(L5), .Q(Q5), .clk(clock), .clr(reset));
  Register #(.width(32)) R6 (.D(DI), .en(L6), .Q(Q6), .clk(clock), .clr(reset));
  Register #(.width(32)) R7 (.D(DI), .en(L7), .Q(Q7), .clk(clock), .clr(reset));
  Register #(.width(32)) R8 (.D(DI), .en(L8), .Q(Q8), .clk(clock), .clr(reset));
  Register #(.width(32)) R9 (.D(DI), .en(L9), .Q(Q9), .clk(clock), .clr(reset));
  Register #(.width(32)) R10 (.D(DI), .en(L10), .Q(Q10), .clk(clock), .clr(reset));
  Register #(.width(32)) R11 (.D(DI), .en(L11), .Q(Q11), .clk(clock), .clr(reset));
  Register #(.width(32)) R12 (.D(DI), .en(L12), .Q(Q12), .clk(clock), .clr(reset));
  Register #(.width(32)) R13 (.D(DI), .en(L13), .Q(Q13), .clk(clock), .clr(reset));
  Register #(.width(32)) R14 (.D(DI), .en(L14), .Q(Q14), .clk(clock), .clr(reset));
  Register #(.width(32)) R15 (.D(DI), .en(L15), .Q(Q15), .clk(clock), .clr(reset));
  Register #(.width(32)) R16 (.D(DI), .en(L16), .Q(Q16), .clk(clock), .clr(reset));
  Register #(.width(32)) R17 (.D(DI), .en(L17), .Q(Q17), .clk(clock), .clr(reset));
  Register #(.width(32)) R18 (.D(DI), .en(L18), .Q(Q18), .clk(clock), .clr(reset));
  Register #(.width(32)) R19 (.D(DI), .en(L19), .Q(Q19), .clk(clock), .clr(reset));
  Register #(.width(32)) R20 (.D(DI), .en(L20), .Q(Q20), .clk(clock), .clr(reset));
  Register #(.width(32)) R21 (.D(DI), .en(L21), .Q(Q21), .clk(clock), .clr(reset));
  Register #(.width(32)) R22 (.D(DI), .en(L22), .Q(Q22), .clk(clock), .clr(reset));
  Register #(.width(32)) R23 (.D(DI), .en(L23), .Q(Q23), .clk(clock), .clr(reset));
  Register #(.width(32)) R24 (.D(DI), .en(L24), .Q(Q24), .clk(clock), .clr(reset));
  Register #(.width(32)) R25 (.D(DI), .en(L25), .Q(Q25), .clk(clock), .clr(reset));
  Register #(.width(32)) R26 (.D(DI), .en(L26), .Q(Q26), .clk(clock), .clr(reset));
  Register #(.width(32)) R27 (.D(DI), .en(L27), .Q(Q27), .clk(clock), .clr(reset));
  Register #(.width(32)) R28 (.D(DI), .en(L28), .Q(Q28), .clk(clock), .clr(reset));
  Register #(.width(32)) R29 (.D(DI), .en(L29), .Q(Q29), .clk(clock), .clr(reset));
  Register #(.width(32)) R30 (.D(DI), .en(L30), .Q(Q30), .clk(clock), .clr(reset));
  Register #(.width(32)) R31_SP (.D(multiplexer_2_out), .en(or_2_out), .Q(SP_Out), .clk(clock), .clr(reset));
  Register #(.width(32)) PC (.D(PC_IN), .en(pc_en), .Q(PC_Out), .clk(clock), .clr(reset));
  Register #(.width(32)) register_1 (.D(I_IN), .en(inst_en), .Q(Instruction), .clk(clock), .clr(reset));
  Random #(.width(32)) random_1 (.clk(clock), .next(random_en), .out(Random));  // open: clr
  Register #(.width(32)) register_2 (.D(Lo), .en(loHi_en), .Q(Lo_2), .clk(clock), .clr(reset));
  Register #(.width(32)) register_3 (.D(Hi), .en(loHi_en), .Q(Hi_2), .clk(clock), .clr(reset));
  Multiplexer #(.select(5), .width(32), .enable("false")) multiplexer_3 (
    .in0(Q0), .in1(Q1), .in2(Q2), .in3(Q3), .in4(Q4), .in5(Q5), .in6(Q6), .in7(Q7), .in8(Q8), .in9(Q9),
    .in10(Q10), .in11(Q11), .in12(Q12), .in13(Q13), .in14(Q14), .in15(Q15), .in16(Q16), .in17(Q17),
    .in18(Q18), .in19(Q19), .in20(Q20), .in21(Q21), .in22(Q22), .in23(Q23), .in24(Q24), .in25(Q25),
    .in26(Q26), .in27(Q27), .in28(Q28), .in29(Q29), .in30(Q30), .in31(SP_Out), .out(A), .sel(S_a));
  Multiplexer #(.select(5), .width(32), .enable("false")) multiplexer_4 (
    .in0(Q0), .in1(Q1), .in2(Q2), .in3(Q3), .in4(Q4), .in5(Q5), .in6(Q6), .in7(Q7), .in8(Q8), .in9(Q9),
    .in10(Q10), .in11(Q11), .in12(Q12), .in13(Q13), .in14(Q14), .in15(Q15), .in16(Q16), .in17(Q17),
    .in18(Q18), .in19(Q19), .in20(Q20), .in21(Q21), .in22(Q22), .in23(Q23), .in24(Q24), .in25(Q25),
    .in26(Q26), .in27(Q27), .in28(Q28), .in29(Q29), .in30(Q30), .in31(SP_Out), .out(B), .sel(S_b));

  // Other names for the same wires on the sheet: clk = clock; i_en = inst_en; I_OUT[31:0] = Instruction;
  //   Q31[31:0] = SP_Out; rst = reset

  // Notes on the sheet:
  //   Input
  //   Register Store
  //   Stack Pointer
  //   Program Counter
  //   Instruction
  //   Random
  //   LoHi
  //   Output
endmodule

module Instruction_Decoder (
  input  [31:0] in_1,
  output [25:0] J,
  output [31:0] cte,
  output [4:0] RS,
  output [4:0] RD,
  output [4:0] RT,
  output bneq,
  output nop,
  output bgtz,
  output beq,
  output blez,
  output lw,
  output bltz,
  output sw,
  output [5:0] func_code,
  output mfhi,
  output [5:0] op_code,
  output mflo,
  output halt,
  output jump,
  output random,
  output jr,
  output tty,
  output keyboard,
  output add,
  output sub,
  output mult,
  output mulu,
  output div,
  output divu,
  output sltu,
  output slt,
  output \and ,
  output \or ,
  output \nor ,
  output \xor ,
  output addi,
  output slti,
  output ori,
  output xori,
  output andi,
  output sltiu,
  output push,
  output pop
);

  wire inmediatly_instr, mem_instr, or_1_out, R_type, special_instr, stack_instr;

  and and_1 (R_type, ~in_1[29], ~in_1[28], ~in_1[27], ~in_1[26]);  // AND_Gate
  and and_2 (stack_instr, in_1[30], ~in_1[26]);  // AND_Gate
  and and_3 (beq, ~in_1[29], in_1[28], ~in_1[27], ~in_1[26]);  // AND_Gate
  and and_4 (bneq, ~in_1[29], in_1[28], ~in_1[27], in_1[26]);  // AND_Gate
  and and_5 (blez, ~in_1[29], in_1[28], in_1[27], ~in_1[26]);  // AND_Gate
  and and_6 (bgtz, ~in_1[29], in_1[28], in_1[27], in_1[26]);  // AND_Gate
  and and_7 (bltz, ~in_1[28], ~in_1[27], in_1[26]);  // AND_Gate
  and and_8 (inmediatly_instr, ~in_1[31], in_1[29]);  // AND_Gate
  and and_9 (jump, ~in_1[31], ~in_1[29], ~in_1[28], in_1[27]);  // AND_Gate
  and and_10 (special_instr, in_1[30], in_1[28]);
  and and_11 (mem_instr, in_1[31], ~in_1[30]);  // AND_Gate
  and and_12 (halt, special_instr, in_1[2], in_1[1], in_1[0]);
  and and_13 (pop, stack_instr, ~in_1[0]);  // AND_Gate
  and and_14 (push, stack_instr, in_1[0]);
  and and_15 (sw, mem_instr, in_1[29]);
  and and_16 (tty, special_instr, ~in_1[2], ~in_1[1], in_1[0]);  // AND_Gate
  and and_17 (keyboard, special_instr, in_1[2], ~in_1[1], ~in_1[0]);  // AND_Gate
  and and_18 (random, special_instr, ~in_1[2], in_1[1], ~in_1[0]);  // AND_Gate
  and and_19 (lw, mem_instr, ~in_1[29]);  // AND_Gate
  and and_20 (jr, R_type, ~in_1[5], ~in_1[4], in_1[3], ~in_1[2], ~in_1[1], ~in_1[0]);  // AND_Gate
  and and_21 (add, R_type, in_1[5], ~in_1[4], ~in_1[3], ~in_1[2], ~in_1[1], ~in_1[0]);  // AND_Gate
  and and_22 (sub, R_type, in_1[5], ~in_1[4], ~in_1[3], ~in_1[2], in_1[1], ~in_1[0]);  // AND_Gate
  and and_23 (mult, R_type, ~in_1[5], in_1[4], in_1[3], ~in_1[2], ~in_1[1], ~in_1[0]);  // AND_Gate
  and and_24 (mulu, R_type, ~in_1[5], in_1[4], in_1[3], ~in_1[2], ~in_1[1], in_1[0]);  // AND_Gate
  and and_25 (div, R_type, ~in_1[5], in_1[4], in_1[3], ~in_1[2], in_1[1], ~in_1[0]);  // AND_Gate
  and and_26 (divu, R_type, ~in_1[5], in_1[4], in_1[3], ~in_1[2], in_1[1], in_1[0]);  // AND_Gate
  and and_27 (slt, R_type, in_1[5], ~in_1[4], in_1[3], ~in_1[2], in_1[1], ~in_1[0]);  // AND_Gate
  and and_28 (sltu, R_type, in_1[5], ~in_1[4], in_1[3], ~in_1[2], in_1[1], in_1[0]);  // AND_Gate
  and and_29 (\and , R_type, in_1[5], ~in_1[4], ~in_1[3], in_1[2], ~in_1[1], ~in_1[0]);  // AND_Gate
  and and_30 (\or , R_type, in_1[5], ~in_1[4], ~in_1[3], in_1[2], ~in_1[1], in_1[0]);  // AND_Gate
  and and_31 (\nor , R_type, in_1[5], ~in_1[4], ~in_1[3], in_1[2], in_1[1], in_1[0]);  // AND_Gate
  and and_32 (\xor , R_type, in_1[5], ~in_1[4], in_1[3], ~in_1[2], ~in_1[1], ~in_1[0]);  // AND_Gate
  and and_33 (mfhi, R_type, ~in_1[5], in_1[4], ~in_1[3], ~in_1[2], ~in_1[1], ~in_1[0]);  // AND_Gate
  and and_34 (mflo, R_type, ~in_1[5], in_1[4], ~in_1[3], ~in_1[2], in_1[1], ~in_1[0]);  // AND_Gate
  and and_35 (nop, R_type, ~in_1[5], ~in_1[4], ~in_1[3], ~in_1[2], ~in_1[1], ~in_1[0]);  // AND_Gate
  and and_36 (addi, inmediatly_instr, ~in_1[28], ~in_1[27], ~in_1[26]);  // AND_Gate
  and and_37 (slti, inmediatly_instr, ~in_1[28], in_1[27], ~in_1[26]);  // AND_Gate
  and and_38 (sltiu, inmediatly_instr, ~in_1[28], in_1[27], in_1[26]);  // AND_Gate
  and and_39 (andi, inmediatly_instr, in_1[28], ~in_1[27], ~in_1[26]);  // AND_Gate
  and and_40 (ori, inmediatly_instr, in_1[28], ~in_1[27], in_1[26]);  // AND_Gate
  and and_41 (xori, inmediatly_instr, in_1[28], in_1[27], ~in_1[26]);  // AND_Gate
  Multiplexer #(.width(32), .enable("false")) multiplexer_1 (
    .in0({{17{in_1[15]}}, in_1[14:0]}), .in1({{16{1'b0}}, in_1[15:0]}), .out(cte), .sel(or_1_out));
  or or_1 (or_1_out, andi, ori, xori);

  assign func_code = in_1[5:0];
  assign J = in_1[25:0];
  assign op_code = in_1[31:26];
  assign RD = in_1[15:11];
  assign RS = in_1[25:21];
  assign RT = in_1[20:16];

  // Other names for the same wires on the sheet: FuncCode[5:0] = in_1[5:0]; i[15:0] = in_1[15:0];
  //   sel_R[5:0] = in_1[5:0]; sel_Special[2:0] = in_1[2:0]; sel_Stack = in_1[0]; sel_LH = in_1[1]; beq_instr = beq;
  //   bgtz_instr = bgtz; blez_instr = blez; bltz_instr = bltz; bneq_instr = bneq; OpCode[5:0] = in_1[31:26]

  // Notes on the sheet:
  //   Input
  //   Data Path Outputs
  //   Special Outputs
  //   ALU Outputs
  //   Stack Outputs
  //   Instruction 
  //   Control Unit Outputs
  //   Jump Outputs
  //   Special Decoder
  //   Stack Decoder
  //   LW/SW Decoder
  //   OpCode Decoder
  //   Inmediatly Decoder
  //   R Decoder
endmodule

module Branch_Control_Unit (
  input  cu_beq,
  input  cu_bne,
  input  cu_blez,
  input  cu_bgtz,
  input  cu_bltz,
  input  cu_j,
  input  cu_jr,
  input  Next,
  input  [31:0] eq,
  input  [31:0] neq,
  input  [31:0] lez,
  input  [31:0] gtz,
  input  [31:0] ltz,
  input  [25:0] Dest,
  input  [31:0] Offset,
  input  [31:0] RS,
  input  [31:0] PC_in,
  output [31:0] PC_Out
);

  wire and_1_out, and_2_out, and_3_out, and_4_out, and_5_out, branch, jmp;
  wire [31:0] BranchAddress, multiplexer_1_out, multiplexer_2_out, PC_4;

  and and_1 (and_1_out, cu_beq, eq[0]);
  and and_2 (and_2_out, neq[0], cu_bne);
  and and_3 (and_3_out, cu_blez, lez[0]);
  and and_4 (and_4_out, cu_bgtz, gtz[0]);
  and and_5 (and_5_out, cu_bltz, ltz[0]);
  Adder #(.width(32)) adder_1 (.a(PC_in), .b(32'h4), .out(PC_4));  // open: cin, cout
  or or_1 (branch, and_1_out, and_2_out, and_3_out, and_4_out, and_5_out);
  Adder #(.width(32)) adder_2 (.a(PC_4), .b({Offset[29:0], 2'b00}), .out(BranchAddress));  // open: cin, cout
  or or_2 (jmp, branch, cu_j, cu_jr);
  Multiplexer #(.select(2), .width(32), .enable("false")) multiplexer_1 (
    .in0(BranchAddress), .in1(RS), .in2({PC_in[31:28], Dest, 2'b00}), .out(multiplexer_1_out),
    .sel({cu_j, cu_jr}));  // open: in3
  Multiplexer #(.width(32), .enable("false")) multiplexer_2 (
    .in0(PC_4), .in1(multiplexer_1_out), .out(multiplexer_2_out), .sel(jmp));
  Multiplexer #(.width(32), .enable("false")) multiplexer_3 (
    .in0(PC_in), .in1(multiplexer_2_out), .out(PC_Out), .sel(Next));

  // Other names for the same wires on the sheet: jr = cu_jr; j = cu_j; beq = cu_beq; bgtz = cu_bgtz; blez = cu_blez;
  //   bltz = cu_bltz; bne = cu_bne; Destination[31:2] = {PC_in[31:28], Dest}; ShiftL_Offset[31:2] = Offset[29:0]

  // Notes on the sheet:
  //   Inputs
endmodule

module Instruction_Fetcher (
  input  [31:0] ram_in_1,
  input  [31:0] ram_in_2,
  input  [31:0] ram_in_3,
  input  [31:0] ram_in_4,
  input  [31:0] pc_out,
  input  clk,
  input  Ready,
  input  clr,
  output [31:0] out_9,
  output Finish
);

  Multiplexer #(.select(2), .width(32), .enable("false")) multiplexer_1 (
    .in0(ram_in_1), .in1(ram_in_2), .in2(ram_in_3), .in3(ram_in_4),
    .out({out_9[7:0], out_9[15:8], out_9[23:16], out_9[31:24]}), .sel(pc_out[3:2]));
  D_Flip_Flop d_ff_1 (.clk(clk), .D(Ready), .Q(Finish));  // open: Qn, preset, en, reset

  // Other names for the same wires on the sheet: Bank[1:0] = pc_out[3:2]
endmodule

module Memory_Handler (
  input  [3:0] ReadTime,
  input  enRead,
  input  clear,
  input  clk,
  input  [3:0] Write_Time,
  input  enWrite,
  input  [31:0] RAM_Out_0,
  input  [31:0] RAM_Out_1,
  input  [31:0] RAM_Out_2,
  input  [31:0] RAM_Out_3,
  input  [31:0] Dir,
  input  [31:0] Value,
  output [31:0] DataOut,
  output CS_R,
  output FinishR,
  output CS_W,
  output FinishW,
  output [31:0] RAM_Input_1,
  output [31:0] RAM_Input_2,
  output [31:0] RAM_Input_3,
  output [31:0] RAM_Input_4,
  output [3:0] mask,
  output [15:0] address
);

  wire wait_time_1_finish;
  wire [31:0] multiplexer_1_out, WD_q;

  Decoder #(.select(2), .enable("false")) decoder_1 (
    .out0(mask[0]), .out1(mask[1]), .out2(mask[2]), .out3(mask[3]), .sel(Dir[3:2]));
  Register #(.width(32)) WD (
    .D({Value[7:0], Value[15:8], Value[23:16], Value[31:24]}), .en(CS_W), .Q(WD_q), .clk(clk), .clr(clear));
  Demultiplexer #(.select(2), .width(32), .enable("false")) demultiplexer_1 (
    .out0(RAM_Input_1), .out1(RAM_Input_2), .out2(RAM_Input_3), .out3(RAM_Input_4), .in(WD_q), .sel(Dir[3:2]));
  Multiplexer #(.select(2), .width(32), .enable("false")) multiplexer_1 (
    .in0(RAM_Out_0), .in1(RAM_Out_1), .in2(RAM_Out_2), .in3(RAM_Out_3), .out(multiplexer_1_out),
    .sel(Dir[3:2]));
  Register #(.width(32)) RD (
    .D({multiplexer_1_out[7:0], multiplexer_1_out[15:8], multiplexer_1_out[23:16], multiplexer_1_out[31:24]}),
    .en(CS_R), .Q(DataOut), .clk(clk), .clr(clear));
  Wait_Time wait_time_1 (
    .\time (ReadTime), .start(enRead), .clk(clk), .clr(clear), .finish(wait_time_1_finish), .cs(CS_R));
  Wait_Time wait_time_2 (.\time (Write_Time), .start(enWrite), .clk(clk), .clr(clear), .finish(FinishW), .cs(CS_W));
  D_Flip_Flop d_ff_1 (.clk(clk), .D(wait_time_1_finish), .Q(FinishR));  // open: Qn, preset, en, reset

  assign address = Dir[19:4];

  // Other names for the same wires on the sheet: Bank[1:0] = Dir[3:2]; RAM_OUTPUT_0[31:0] = RAM_Out_0;
  //   RAM_OUTPUT_1[31:0] = RAM_Out_1; RAM_OUTPUT_2[31:0] = RAM_Out_2; RAM_OUTPUT_3[31:0] = RAM_Out_3;
  //   Read_Time[3:0] = ReadTime

  // Notes on the sheet:
  //   RAM TIMING
  //   DATA FROM RAM
endmodule

module Wait_Time (
  input  [3:0] \time ,
  input  start,
  input  clk,
  input  clr,
  output finish,
  output cs
);

  wire Count__0, CS1, d_ff_1_q, Load;
  wire [3:0] counter_1_q, multiplexer_1_out;

  or or_1 (cs, CS1, finish);
  or or_2 (Load, CS1, start);
  Multiplexer #(.width(4), .enable("false")) multiplexer_1 (
    .in0(4'b0001), .in1(\time ), .out(multiplexer_1_out), .sel(start));
  Counter #(.width(4), .max('hf)) counter_1 (
    .load(Load), .D(multiplexer_1_out), .count(CS1), .Q(counter_1_q), .clk(clk));  // open: carry, clr
  Demultiplexer #(.enable("false")) demultiplexer_1 (.out0(CS1), .out1(finish), .in(d_ff_1_q), .sel(Count__0));
  D_Flip_Flop d_ff_1 (.clk(clk), .D(Load), .Q(d_ff_1_q));  // open: Qn, preset, en, reset
  Comparator #(.width(4)) comparator_1 (.a(counter_1_q), .b(4'b0000), .eq(Count__0));  // open: gt, lt

  // Other names for the same wires on the sheet: CS2 = finish; Dec = CS1
endmodule

module Control_Unit (
  input  nop,
  input  divu,
  input  pop,
  input  halt,
  input  andi,
  input  sw,
  input  ready_mem,
  input  ready_inst,
  input  add,
  input  \and ,
  input  slt,
  input  kbd,
  input  ori,
  input  beq,
  input  CLK,
  input  sub,
  input  \or ,
  input  sltu,
  input  rnd,
  input  xori,
  input  bne,
  input  mul,
  input  \nor ,
  input  jr,
  input  tty,
  input  slti,
  input  blez,
  input  mulu,
  input  \xor ,
  input  mfhi,
  input  j,
  input  sltiu,
  input  bgtz,
  input  div,
  input  push,
  input  mflo,
  input  addi,
  input  lw,
  input  bltz,
  output Next,
  output [2:0] OpCode,
  output Sign,
  output beq_2,
  output bne_2,
  output blez_2,
  output bgtz_2,
  output bltz_2,
  output j_2,
  output jr_2,
  output enRND,
  output STOP,
  output enRead,
  output enWrite,
  output pushRF,
  output popRF,
  output enSP,
  output R_W,
  output InstEnab,
  output TTYEnab,
  output KBDEnab
);

  wire _0, _0_t, _0_t_t, _0_t_t_t, _0_t_t_t_t, _0_t_t_t_t_t, _0_t_t_t_t_t_t, _1, _1_t, _1_t_t, _1_t_t_t,
       _1_t_t_t_t, _1_t_t_t_t_t, _1_t_t_t_t_t_t, _2, _2_t, _3, _4, and_37_out, d_ff_2_q, d_ff_2_qn,
       demultiplexer_1_out0, En, En_8, EnRead_0, EnRead_1, EnWrt_0, EnWrt_1, j_end, jr_end, mfhi_end,
       mflo_end, NextInst, nop_end, or_9_out, or_13_out, R__W_14, R__W_15, R__W_16, R__W_17, Sel, tunnel_t,
       tunnel_t_t, tunnel_t_t_t, tunnel_t_t_t_t, tunnel_t_t_t_t_t, tunnel_t_t_t_t_t_t, tunnel_t_t_t_t_t_t_t;
  wire [2:0] priority_encoder_1_out;

  Priority_Encoder priority_encoder_1 (
    .in0(tunnel_t_t_t), .in1(tunnel_t_t_t_t), .in2(tunnel_t), .in3(En_8), .in4(tunnel_t_t_t_t_t_t_t),
    .in5(tunnel_t_t_t_t_t_t), .in6(tunnel_t_t), .in7(tunnel_t_t_t_t_t), .out(priority_encoder_1_out),
    .en_in(En));  // open: gs, en_out
  and and_1 (_0_t_t, NextInst, add);
  and and_2 (_0_t_t_t, NextInst, sub);
  and and_3 (_0_t, NextInst, mul);
  and and_4 (_1_t, NextInst, mulu);
  and and_5 (_0_t_t_t_t, NextInst, div);
  and and_6 (_1_t_t_t_t, NextInst, divu);
  and and_7 (_0, NextInst, \and );
  and and_8 (_0_t_t_t_t_t_t, NextInst, \or );
  and and_9 (En_8, NextInst, \nor );
  and and_10 (_0_t_t_t_t_t, NextInst, \xor );
  and and_11 (_1_t_t, NextInst, addi);
  and and_12 (_1, NextInst, andi);
  and and_13 (_1_t_t_t_t_t_t, NextInst, ori);
  and and_14 (_1_t_t_t_t_t, NextInst, xori);
  and and_15 (R__W_14, NextInst, slt);
  and and_16 (R__W_15, NextInst, sltu);
  and and_17 (R__W_16, NextInst, slti);
  and and_18 (R__W_17, NextInst, sltiu);
  and and_19 (jr_end, NextInst, jr);
  and and_20 (_1_t_t_t, NextInst, beq);
  and and_21 (_2_t, NextInst, bne);
  and and_22 (_2, NextInst, blez);
  and and_23 (_3, NextInst, bgtz);
  and and_24 (_4, NextInst, bltz);
  and and_25 (mfhi_end, NextInst, mfhi);
  and and_26 (mflo_end, NextInst, mflo);
  and and_27 (enRND, NextInst, rnd);
  and and_28 (STOP, NextInst, halt);
  and and_29 (EnRead_0, NextInst, pop);
  and and_30 (pushRF, NextInst, push);
  and and_31 (EnRead_1, NextInst, lw);
  and and_32 (EnWrt_1, NextInst, sw);
  and and_33 (nop_end, NextInst, nop);
  and and_34 (j_end, NextInst, j);
  and and_35 (TTYEnab, NextInst, tty);
  and and_36 (KBDEnab, NextInst, kbd);
  Multiplexer #(.width(3), .enable("false")) multiplexer_1 (
    .in0(priority_encoder_1_out), .in1(3'b000), .out(OpCode), .sel(Sel));
  and and_37 (and_37_out, ~EnWrt_0, pushRF);  // AND_Gate
  or or_1 (tunnel_t_t_t, _0_t_t, _1_t_t, _2, _3, _4);
  or or_2 (tunnel_t_t_t_t, _0_t_t_t, _1_t_t_t, _2_t);
  or or_3 (tunnel_t_t, _0_t, _1_t);
  or or_4 (tunnel_t_t_t_t_t, _0_t_t_t_t, _1_t_t_t_t);
  or or_5 (tunnel_t, _0, _1);
  or or_6 (tunnel_t_t_t_t_t_t_t, _0_t_t_t_t_t_t, _1_t_t_t_t_t_t);
  or or_7 (tunnel_t_t_t_t_t_t, _0_t_t_t_t_t, _1_t_t_t_t_t);
  D_Flip_Flop d_ff_1 (.clk(CLK), .D(and_37_out), .Q(EnWrt_0));  // open: Qn, preset, en, reset
  or or_8 (En, _0_t_t, _0_t_t_t, _0_t, _1_t, _0_t_t_t_t, _1_t_t_t_t, _0, _0_t_t_t_t_t_t, En_8, _0_t_t_t_t_t, _1_t_t, _1, _1_t_t_t_t_t_t, _1_t_t_t_t_t, _1_t_t_t, _2_t, _2, _3, _4);
  and and_38 (popRF, ready_mem, pop);
  D_Flip_Flop d_ff_2 (.clk(CLK), .D(or_9_out), .Q(d_ff_2_q), .Qn(d_ff_2_qn), .preset(d_ff_2_qn));  // open: en, reset
  or or_9 (or_9_out, demultiplexer_1_out0, Next);
  or or_10 (Sign, _0_t, _0_t_t_t_t, R__W_14, R__W_16, _1_t_t_t, _2_t, _2, _3, _4);
  or or_11 (enRead, EnRead_0, EnRead_1);
  or or_12 (enWrite, EnWrt_0, EnWrt_1);
  Demultiplexer #(.enable("false")) demultiplexer_1 (
    .out0(demultiplexer_1_out0), .out1(InstEnab), .in(d_ff_2_q), .sel(or_13_out));
  or or_13 (or_13_out, ready_inst, ready_mem);
  or or_14 (R_W, _0_t_t, _0_t_t_t, _0_t, _1_t, _0_t_t_t_t, _1_t_t_t_t, _0, _0_t_t_t_t_t_t, En_8, _0_t_t_t_t_t, _1_t_t, _1, _1_t_t_t_t_t_t, _1_t_t_t_t_t, R__W_14, R__W_15, R__W_16, R__W_17, jr_end, mfhi_end, mflo_end, popRF, lw, KBDEnab, enRND);
  and and_39 (NextInst, InstEnab, ~ready_mem);  // AND_Gate
  or or_15 (enSP, popRF, pushRF);
  nor nor_1 (Sel, tunnel_t_t_t, tunnel_t_t_t_t, tunnel_t, En_8, tunnel_t_t_t_t_t_t_t, tunnel_t_t_t_t_t_t, tunnel_t_t, tunnel_t_t_t_t_t);
  or or_16 (Next, mflo_end, nop_end, _0_t_t, _0_t_t_t, _0_t, _1_t, _0_t_t_t_t, _1_t_t_t_t, _0, _0_t_t_t_t_t_t, En_8, _0_t_t_t_t_t, _1_t_t, _1, _1_t_t_t_t_t_t, _1_t_t_t_t_t, R__W_14, R__W_15, R__W_16, R__W_17, jr_end, j_end, _1_t_t_t, _2_t, _2, _3, _4, STOP, enRND, mfhi_end, KBDEnab, TTYEnab);

  assign beq_2 = beq;
  assign bgtz_2 = bgtz;
  assign blez_2 = blez;
  assign bltz_2 = bltz;
  assign bne_2 = bne;
  assign j_2 = j;
  assign jr_2 = jr;

  // Other names for the same wires on the sheet: En_7 = _0_t_t_t_t_t_t; or_end = _0_t_t_t_t_t_t;
  //   R__W_7 = _0_t_t_t_t_t_t; En_12 = _1_t_t_t_t_t_t; ori_end = _1_t_t_t_t_t_t; R__W_12 = _1_t_t_t_t_t_t;
  //   add_end = _0_t_t; En_0 = _0_t_t; R__W_0 = _0_t_t; addi_end = _1_t_t; En_10 = _1_t_t; R__W_10 = _1_t_t;
  //   and_end = _0; En_6 = _0; R__W_6 = _0; andi_end = _1; En_11 = _1; R__W_11 = _1; beq_end = _1_t_t_t;
  //   En_14 = _1_t_t_t; Sign_4 = _1_t_t_t; bgtz_end = _3; En_17 = _3; Sign_7 = _3; blez_end = _2; En_16 = _2;
  //   Sign_6 = _2; bltz_end = _4; En_18 = _4; Sign_8 = _4; bne_end = _2_t; En_15 = _2_t; Sign_5 = _2_t;
  //   div_end = _0_t_t_t_t; En_4 = _0_t_t_t_t; R__W_4 = _0_t_t_t_t; Sign_1 = _0_t_t_t_t; divu_end = _1_t_t_t_t;
  //   En_5 = _1_t_t_t_t; R__W_5 = _1_t_t_t_t; enSP_0 = popRF; R_W_21 = popRF; enSP_1 = pushRF; EnWrt = enWrite;
  //   halt_end = STOP; R__W_18 = jr_end; kbd_enab = KBDEnab; kbd_end = KBDEnab; R_W_23 = KBDEnab; lw_end = EnRead_1;
  //   mem_ready = ready_mem; R_W_19 = mfhi_end; R_W_20 = mflo_end; En_2 = _0_t; mul_end = _0_t; R__W_2 = _0_t;
  //   Sign_0 = _0_t; En_3 = _1_t; mulu_end = _1_t; R__W_3 = _1_t; nor_end = En_8; R__W_8 = En_8; tunnel = En_8;
  //   pop_end = EnRead_0; push_end = EnWrt_0; R__W = R_W; R_W_22 = lw; R_W_24 = enRND; rnd_end = enRND;
  //   Sign_2 = R__W_14; slt_end = R__W_14; Sign_3 = R__W_16; slti_end = R__W_16; sltiu_end = R__W_17;
  //   sltu_end = R__W_15; En_1 = _0_t_t_t; R__W_1 = _0_t_t_t; sub_end = _0_t_t_t; sw_end = EnWrt_1;
  //   time_ready = ready_inst; tty_enab = TTYEnab; tty_end = TTYEnab; En_9 = _0_t_t_t_t_t; R__W_9 = _0_t_t_t_t_t;
  //   xor_end = _0_t_t_t_t_t; En_13 = _1_t_t_t_t_t; R__W_13 = _1_t_t_t_t_t; xori_end = _1_t_t_t_t_t
endmodule

module Instruction_Cache (
  input  [31:0] Address,
  input  enable,
  input  clear,
  input  clk,
  input  [31:0] RAM_Out_0,
  input  [31:0] RAM_Out_1,
  input  [31:0] RAM_Out_2,
  input  [31:0] RAM_Out_3,
  input  [3:0] ReadTime,
  output CS,
  output Finish,
  output [31:0] CacheOut0,
  output [31:0] CacheOut1,
  output [31:0] CacheOut2,
  output [31:0] CacheOut3,
  output [15:0] AddressOut
);

  wire comparator_1_eq, controlled_buffer_1_out, controlled_buffer_2_out, controlled_buffer_3_out,
       controlled_buffer_4_out, controlled_buffer_5_out, controlled_buffer_6_out, controlled_buffer_7_out,
       controlled_buffer_8_out, decoder_1_out0, decoder_1_out1, decoder_1_out2, decoder_1_out3,
       decoder_1_out4, decoder_1_out5, decoder_1_out6, decoder_1_out7, demultiplexer_1_out0,
       demultiplexer_2_out0, demultiplexer_2_out1, Finish_t, hit, miss, not_2_out, not_3_out, not_4_out,
       not_5_out, not_6_out, not_7_out, not_8_out, not_9_out, or_1_out, Ready, start, start_q, v0, v1, v2,
       v3, v4, v5, v6, v7, Val, wait_q;
  wire [12:0] tagOut;

  RAM_part #(.addrWidth(3), .dataWidth(32), .bus("separate")) ram_1 (
    .addr(Address[6:4]), .din(RAM_Out_0), .data(CacheOut0), .str(Finish_t), .clk(clk), .ld(1'b1), .clr(clear));  // open: sel
  RAM_part #(.addrWidth(3), .dataWidth(32), .bus("separate")) ram_2 (
    .addr(Address[6:4]), .din(RAM_Out_1), .data(CacheOut1), .str(Finish_t), .clk(clk), .ld(1'b1), .clr(clear));  // open: sel
  RAM_part #(.addrWidth(3), .dataWidth(32), .bus("separate")) ram_3 (
    .addr(Address[6:4]), .din(RAM_Out_2), .data(CacheOut2), .str(Finish_t), .clk(clk), .ld(1'b1), .clr(clear));  // open: sel
  RAM_part #(.addrWidth(3), .dataWidth(32), .bus("separate")) ram_4 (
    .addr(Address[6:4]), .din(RAM_Out_3), .data(CacheOut3), .str(Finish_t), .clk(clk), .ld(1'b1), .clr(clear));  // open: sel
  RAM_part #(.addrWidth(3), .dataWidth(13), .bus("separate")) ram_5 (
    .addr(Address[6:4]), .din(Address[19:7]), .data(tagOut), .str(Finish_t), .clk(clk), .ld(1'b1), .clr(clear));  // open: sel
  Multiplexer #(.select(3), .enable("false")) multiplexer_1 (
    .in0(v0), .in1(v1), .in2(v2), .in3(v3), .in4(v4), .in5(v5), .in6(v6), .in7(v7), .out(Val),
    .sel(Address[6:4]));
  Comparator #(.width(13), .mode("unsigned")) comparator_1 (
    .a(tagOut), .b(Address[19:7]), .eq(comparator_1_eq));  // open: gt, lt
  and and_1 (hit, Val, comparator_1_eq);
  Demultiplexer #(.enable("false")) demultiplexer_1 (
    .out0(demultiplexer_1_out0), .out1(start), .in(start_q), .sel(miss));
  D_Flip_Flop u_start (.clk(clk), .D(enable), .Q(start_q));  // open: Qn, preset, en, reset
  not not_1 (miss, hit);
  Wait_Time wait_time_1 (.\time (ReadTime), .start(start), .clk(clk), .clr(clear), .finish(Finish_t), .cs(CS));
  or or_1 (or_1_out, demultiplexer_2_out0, start);
  D_Flip_Flop \wait  (.clk(clk), .D(or_1_out), .Q(wait_q));  // open: Qn, preset, en, reset
  Decoder #(.select(3), .enable("false")) decoder_1 (
    .out0(decoder_1_out0), .out1(decoder_1_out1), .out2(decoder_1_out2), .out3(decoder_1_out3),
    .out4(decoder_1_out4), .out5(decoder_1_out5), .out6(decoder_1_out6), .out7(decoder_1_out7),
    .sel(Address[6:4]));
  Demultiplexer #(.enable("false")) demultiplexer_2 (
    .out0(demultiplexer_2_out0), .out1(demultiplexer_2_out1), .in(wait_q), .sel(Finish_t));
  D_Flip_Flop d_ff_1 (.clk(clk), .D(Ready), .Q(Finish));  // open: Qn, preset, en, reset
  or or_2 (Ready, demultiplexer_1_out0, demultiplexer_2_out1);
  not not_2 (not_2_out, v0);
  assign controlled_buffer_1_out = not_2_out ? decoder_1_out0 : 1'bz;  // Controlled_Buffer controlled_buffer_1
  not not_3 (not_3_out, v1);
  assign controlled_buffer_2_out = not_3_out ? decoder_1_out1 : 1'bz;  // Controlled_Buffer controlled_buffer_2
  not not_4 (not_4_out, v2);
  assign controlled_buffer_3_out = not_4_out ? decoder_1_out2 : 1'bz;  // Controlled_Buffer controlled_buffer_3
  not not_5 (not_5_out, v3);
  assign controlled_buffer_4_out = not_5_out ? decoder_1_out3 : 1'bz;  // Controlled_Buffer controlled_buffer_4
  not not_6 (not_6_out, v4);
  assign controlled_buffer_5_out = not_6_out ? decoder_1_out4 : 1'bz;  // Controlled_Buffer controlled_buffer_5
  not not_7 (not_7_out, v5);
  assign controlled_buffer_6_out = not_7_out ? decoder_1_out5 : 1'bz;  // Controlled_Buffer controlled_buffer_6
  not not_8 (not_8_out, v6);
  assign controlled_buffer_7_out = not_8_out ? decoder_1_out6 : 1'bz;  // Controlled_Buffer controlled_buffer_7
  not not_9 (not_9_out, v7);
  assign controlled_buffer_8_out = not_9_out ? decoder_1_out7 : 1'bz;  // Controlled_Buffer controlled_buffer_8
  D_Flip_Flop d_ff_2 (.clk(clk), .D(controlled_buffer_1_out), .Q(v0), .reset(clear));  // open: Qn, preset, en
  D_Flip_Flop d_ff_3 (.clk(clk), .D(controlled_buffer_2_out), .Q(v1), .reset(clear));  // open: Qn, preset, en
  D_Flip_Flop d_ff_4 (.clk(clk), .D(controlled_buffer_3_out), .Q(v2), .reset(clear));  // open: Qn, preset, en
  D_Flip_Flop d_ff_5 (.clk(clk), .D(controlled_buffer_4_out), .Q(v3), .reset(clear));  // open: Qn, preset, en
  D_Flip_Flop d_ff_6 (.clk(clk), .D(controlled_buffer_5_out), .Q(v4), .reset(clear));  // open: Qn, preset, en
  D_Flip_Flop d_ff_7 (.clk(clk), .D(controlled_buffer_6_out), .Q(v5), .reset(clear));  // open: Qn, preset, en
  D_Flip_Flop d_ff_8 (.clk(clk), .D(controlled_buffer_7_out), .Q(v6), .reset(clear));  // open: Qn, preset, en
  D_Flip_Flop d_ff_9 (.clk(clk), .D(controlled_buffer_8_out), .Q(v7), .reset(clear));  // open: Qn, preset, en

  assign AddressOut = Address[19:4];

  // Other names for the same wires on the sheet: offset[1:0] = Address[3:2]; Address_t[15:0] = Address[19:4];
  //   idx[2:0] = Address[6:4]; tag[12:0] = Address[19:7]; RAM_OUTPUT_0[31:0] = RAM_Out_0;
  //   RAM_OUTPUT_1[31:0] = RAM_Out_1; RAM_OUTPUT_2[31:0] = RAM_Out_2; RAM_OUTPUT_3[31:0] = RAM_Out_3;
  //   Read_Time[3:0] = ReadTime

  // Notes on the sheet:
  //   DATA FROM RAM
  //   RAM TIMING
  //   Bank 0
  //   Bank 1
  //   Bank 2
  //   Bank 3
  //   Tag
endmodule
